# Fritzing sketch LCD (saved by Fritzing 0.9.3b)
breadboards: 1

parts:
  Part1 = Arduino Uno (Rev3)
  LCM1602_IIC1 = LCM1602 IIC [part_number="LCM1602 IIC" chip_label="LCM1602 IIC" package="DIP (Dual Inline) [THT]"]
  U1 = LCD-16X2 [package=lcd-16x2_nosilk]

nets:
  N1: Part1.A4/SDA, LCM1602_IIC1.SDA
  N2: Part1.A5/SCL, LCM1602_IIC1.SCL
  5V: Part1.5V, LCM1602_IIC1.VCC
  GND: Part1.GND, LCM1602_IIC1.GND
  VSS: LCM1602_IIC1.VSS, U1.VSS
  VDD: LCM1602_IIC1.VDD, U1.VDD
  N3: LCM1602_IIC1.V0, U1.VO
  N4: LCM1602_IIC1.RS, U1.RS
  N5: LCM1602_IIC1.RW, U1.R_W
  N6: LCM1602_IIC1.E, U1.E
  N7: LCM1602_IIC1.D0, U1.DB0
  N8: LCM1602_IIC1.D1, U1.DB1
  N9: LCM1602_IIC1.D2, U1.DB2
  N10: LCM1602_IIC1.D3, U1.DB3
  N11: LCM1602_IIC1.D4, U1.DB4
  N12: LCM1602_IIC1.D5, U1.DB5
  N13: LCM1602_IIC1.D6, U1.DB6
  N14: LCM1602_IIC1.D7, U1.DB7
  N15: LCM1602_IIC1.A, U1.A
  N16: LCM1602_IIC1.K, U1.K

custom parts:
  LCM1602 IIC: I2C-Module to use a 1602 or 2004 LCD on with the wire.h libory Serial LCD Modul
